# Fritzing sketch res16_pcb_cleaned (saved by Fritzing 0.9.2b)
circuit board: 7.69cm x 4.9cm
breadboards: 6

parts:
  R1 = Resistor [tolerance=±5% resistance=10k package=THT]
  C1 = Capacitor Polarized [package=cpol-radial-100uf-25v]
  R2 = Resistor [tolerance=±5% resistance=100 package=THT]
  header_analogs = female pin header, 14 pins [form="♀ (female)"]
  drv_right = female pin header, 8 pins [form="♀ (female)"]
  drv_left = female pin header, 8 pins [form="♀ (female)"]
  2B2A = Screw terminal - 2 pins [package=THT]
  1A1B = Screw terminal - 2 pins [package=THT]
  header_digitals = female pin header, 14 pins [form="♀ (female)"]
  VREG = Voltage Regulator - 5V [package="TO220 [THT]"]
  AUDIO = Audio Jack (TRS) 3.5mm [package="PG203J [THT]"]  # not connected
  SENSORS = screw terminal, 4 pins
  TDA2030 = screw terminal, 3 pins
  PROTOGRIDxGND = female pin header, 7 pins [form="♀ (female)"]
  12V = Screw terminal - 2 pins [package=THT]
  PROTOGRIDxV = female pin header, 7 pins [form="♀ (female)"]
  AUDIO_GND1 = female pin header, 1 pin [form="♀ (female)"]
  AUDIO_LINE = female pin header, 1 pin [form="♀ (female)"]
  AUDIO_GND2 = female pin header, 1 pin [form="♀ (female)"]

nets:
  N1: R1.Pin_0, header_analogs.pin13, SENSORS.pin2
  N2: R1.Pin_1, C1.+, drv_right.pin2, drv_right.pin8, header_digitals.pin1, VREG.GND, SENSORS.pin4, TDA2030.pin2, PROTOGRIDxGND.pin1, PROTOGRIDxGND.pin2, PROTOGRIDxGND.pin3, PROTOGRIDxGND.pin4, PROTOGRIDxGND.pin5, PROTOGRIDxGND.pin6, PROTOGRIDxGND.pin7, 12V.pin2, AUDIO_GND1.pin1, AUDIO_GND2.pin1
  N3: C1.-, drv_right.pin1, VREG.input_voltage, TDA2030.pin1, 12V.pin1
  N4: R2.Pin_0, header_digitals.pin7
  N5: R2.Pin_1, SENSORS.pin1
  N6: header_analogs.pin1, drv_left.pin2, drv_left.pin4, drv_left.pin5, drv_left.pin6, VREG.output_voltage, SENSORS.pin3, PROTOGRIDxV.pin1, PROTOGRIDxV.pin2, PROTOGRIDxV.pin3, PROTOGRIDxV.pin4, PROTOGRIDxV.pin5, PROTOGRIDxV.pin6, PROTOGRIDxV.pin7
  N7: drv_right.pin3, 2B2A.pin2
  N8: drv_right.pin4, 2B2A.pin1
  N9: drv_right.pin5, 1A1B.pin2
  N10: drv_right.pin6, 1A1B.pin1
  N11: drv_left.pin7, header_digitals.pin6
  N12: drv_left.pin8, header_digitals.pin5
  N13: TDA2030.pin3, AUDIO_LINE.pin1
