# Fritzing sketch res16_pcb_construct_notclean (saved by Fritzing 0.9.2b)
circuit board: 7.7cm x 5cm
breadboards: 6

parts:
  LDR = Photocell (LDR) [package=THT]  # not connected
  LED1 = LED - 3mm [color="White (4500K)" package="3 mm [THT]"]  # not connected
  R1 = Resistor [tolerance=±5% resistance=10k package=THT]
  C1 = Capacitor Polarized [package=cpol-radial-100uf-25v]
  R2 = Resistor [tolerance=±5% resistance=100 package=THT]
  Teensy_3_1 = Teensy 3.1
  header_analogs = female pin header, 14 pins [form="♀ (female)"]
  drv_right = female pin header, 8 pins [form="♀ (female)"]
  DRV_1 = DRV 8825 Stepper Motor Carrier, High Current [part_number="DRV 8825"]
  drv_left = female pin header, 8 pins [form="♀ (female)"]
  2B2A = Screw terminal - 2 pins [package=THT]
  1A1B = Screw terminal - 2 pins [package=THT]
  header_digitals = female pin header, 14 pins [form="♀ (female)"]
  VREG = Voltage Regulator - 5V [package="TO220 [THT]"]
  AUDIO = Audio Jack (TRS) 3.5mm [package="PG203J [THT]"]
  sensor_terminal = screw terminal, 4 pins
  TDA2030 = screw terminal, 3 pins
  grid_y = female pin header, 12 pins [form="♀ (female)"]  # not connected
  grid_x_holder = female pin header, 27 pins [form="♀ (female)"]  # not connected
  PROTOGRIDxGND = female pin header, 7 pins [form="♀ (female)"]
  12V = Screw terminal - 2 pins [package=THT]

nets:
  N1: R1.Pin_0, Teensy_3_1.A0/D14, header_analogs.pin13, sensor_terminal.pin4
  GND: R1.Pin_1, C1.+, Teensy_3_1.GND, drv_right.pin2, drv_right.pin8, DRV_1.GROUND_ST/_MT, DRV_1.GROUND_LOG, header_digitals.pin1, VREG.GND, AUDIO.Sleeve, AUDIO.Tip, sensor_terminal.pin1, TDA2030.pin2, TDA2030.pin3, PROTOGRIDxGND.pin1, PROTOGRIDxGND.pin2, PROTOGRIDxGND.pin3, PROTOGRIDxGND.pin4, PROTOGRIDxGND.pin5, PROTOGRIDxGND.pin6, PROTOGRIDxGND.pin7, 12V.pin2
  N2: C1.-, drv_right.pin1, DRV_1.VOLTAGE_ST/_MT, VREG.input_voltage, TDA2030.pin1, 12V.pin1
  N3: R2.Pin_0, Teensy_3_1.D5, header_digitals.pin7
  N4: R2.Pin_1, sensor_terminal.pin2
  N5: Teensy_3_1.D0, header_digitals.pin2
  N6: Teensy_3_1.D1, header_digitals.pin3
  N7: Teensy_3_1.D2, header_digitals.pin4
  N8: Teensy_3_1.D3, DRV_1.DIRECTION, drv_left.pin8, header_digitals.pin5
  N9: Teensy_3_1.D4, DRV_1.STEP, drv_left.pin7, header_digitals.pin6
  N10: Teensy_3_1.D6, header_digitals.pin8
  N11: Teensy_3_1.D7, header_digitals.pin9
  N12: Teensy_3_1.D8, header_digitals.pin10
  N13: Teensy_3_1.D9, header_digitals.pin11
  N14: Teensy_3_1.D10, header_digitals.pin12
  N15: Teensy_3_1.D11, header_digitals.pin13
  N16: Teensy_3_1.D12, header_digitals.pin14
  N17: Teensy_3_1.3V3, header_analogs.pin3, DRV_1.MS1, DRV_1.MS3, DRV_1.RESET, DRV_1.SLEEP, drv_left.pin2, drv_left.pin4, drv_left.pin5, drv_left.pin6
  N18: Teensy_3_1.A1/D15, header_analogs.pin12
  N19: Teensy_3_1.A2/D16, header_analogs.pin11
  N20: Teensy_3_1.A3/D17, header_analogs.pin10
  N21: Teensy_3_1.A4/D18, header_analogs.pin9
  N22: Teensy_3_1.A5/D19, header_analogs.pin8
  N23: Teensy_3_1.A6/D20, header_analogs.pin7
  N24: Teensy_3_1.A7/D21, header_analogs.pin6
  N25: Teensy_3_1.A8/D22, header_analogs.pin5
  N26: Teensy_3_1.A9/D23, header_analogs.pin4
  N27: Teensy_3_1.AGND, header_analogs.pin2
  N28: Teensy_3_1.Vin, header_analogs.pin1, VREG.output_voltage, sensor_terminal.pin3
  N29: drv_right.pin3, DRV_1.OUT_2B, 2B2A.pin1
  N30: drv_right.pin4, DRV_1.OUT_2A, 2B2A.pin2
  N31: drv_right.pin5, DRV_1.OUT_1A, 1A1B.pin1
  N32: drv_right.pin6, DRV_1.OUT_1B, 1A1B.pin2
  N33: drv_right.pin7, DRV_1.VOLTAGE_DD
  N34: DRV_1.ENABLE, drv_left.pin1
  N35: DRV_1.MS2, drv_left.pin3
